// Digital circuit 4BIT_CPU_Circuit.dig as structural Verilog
module _4BIT_CPU_Circuit (
  input  Clock,
  input  Load_Address,
  input  [3:0] Address_Jump,
  input  [1:0] Register_Selector,
  input  [3:0] Operation_Data,
  output [3:0] out_2,
  output SLT,
  output Zero,
  output [3:0] Output,
  output Carry
);

  wire _4bit_fulladdersubtractor_1_carry, demultiplexer_1_out_0, demultiplexer_1_out_1,
       demultiplexer_1_out_2, demultiplexer_1_out_3, not_1_out, not_2_out;
  wire [3:0] _4bit_fulladdersubtractor_1_sum, A_q, B_q, demultiplexer_2_out_0, demultiplexer_2_out_1,
       demultiplexer_2_out_2, demultiplexer_2_out_3, IR_q, multiplexer_1_out, RAM_16__4_d;

  _4bit_fullAdderSubtractor _4bit_fulladdersubtractor_1 (
    .A(out_2), .B(4'b0001), .C_in(1'b0), .Sum(_4bit_fulladdersubtractor_1_sum),
    .Carry(_4bit_fulladdersubtractor_1_carry));
  not not_1 (not_1_out, Clock);
  Multiplexer #(.Bits(4)) multiplexer_1 (
    .sel(Load_Address), .in_0(_4bit_fulladdersubtractor_1_sum), .in_1(Address_Jump), .out(multiplexer_1_out));
  Register #(.Bits(4)) PC (.D(multiplexer_1_out), .C(not_1_out), .en(not_1_out), .Q(out_2));
  BlockRAMDualPort #(.AddrBits(4), .Bits(4)) RAM_16__4 (
    .A(out_2), .Din(Operation_Data), .str(Clock), .C(Clock), .D(RAM_16__4_d));
  not not_2 (not_2_out, Clock);
  Demultiplexer #(.Selector_Bits(2)) demultiplexer_1 (
    .sel(Register_Selector), .in(1'b1), .out_0(demultiplexer_1_out_0), .out_1(demultiplexer_1_out_1),
    .out_2(demultiplexer_1_out_2), .out_3(demultiplexer_1_out_3));
  Demultiplexer #(.Bits(4), .Selector_Bits(2)) demultiplexer_2 (
    .sel(Register_Selector), .in(RAM_16__4_d), .out_0(demultiplexer_2_out_0), .out_1(demultiplexer_2_out_1),
    .out_2(demultiplexer_2_out_2), .out_3(demultiplexer_2_out_3));
  Register #(.Bits(4)) IR (.D(demultiplexer_2_out_0), .C(not_2_out), .en(demultiplexer_1_out_0), .Q(IR_q));
  Register #(.Bits(4)) A (.D(demultiplexer_2_out_1), .C(not_2_out), .en(demultiplexer_1_out_1), .Q(A_q));
  Register #(.Bits(4)) B (.D(demultiplexer_2_out_2), .C(not_2_out), .en(demultiplexer_1_out_2), .Q(B_q));
  FullALU fullalu_1 (
    .A(A_q), .B(B_q), .Selector(IR_q[2:0]), .Output(Output), .Carry(Carry), .Zero_Flag(Zero), .SLT_Flag(SLT));
  // also tied to GND on the sheet: {_4bit_fulladdersubtractor_1_carry, demultiplexer_2_out_3[0], demultiplexer_2_out_3[1], demultiplexer_2_out_3[2], demultiplexer_2_out_3[3], demultiplexer_1_out_3, IR_q[3]}
endmodule
