// Digital circuit 4bit_ALU.dlogic.dig as structural Verilog
module _4bit_ALU_dlogic (
  input  [3:0] A,
  input  [3:0] B,
  input  C_in,
  output [3:0] Sum,
  output Carry
);

  wire _1bit_fulladder_1_carry, _1bit_fulladder_2_carry, _1bit_fulladder_3_carry;

  _1bit_fullAdder _1bit_fulladder_1 (.A(A[0]), .B(B[0]), .C_in(C_in), .Sum(Sum[0]), .Carry(_1bit_fulladder_1_carry));
  _1bit_fullAdder _1bit_fulladder_2 (
    .A(A[1]), .B(B[1]), .C_in(_1bit_fulladder_1_carry), .Sum(Sum[1]), .Carry(_1bit_fulladder_2_carry));
  _1bit_fullAdder _1bit_fulladder_3 (
    .A(A[2]), .B(B[2]), .C_in(_1bit_fulladder_2_carry), .Sum(Sum[2]), .Carry(_1bit_fulladder_3_carry));
  _1bit_fullAdder _1bit_fulladder_4 (.A(A[3]), .B(B[3]), .C_in(_1bit_fulladder_3_carry), .Sum(Sum[3]), .Carry(Carry));
endmodule
