// Digital circuit 4bit_fullAdderSubtractor.dig as structural Verilog
module _4bit_fullAdderSubtractor (
  input  [3:0] A,
  input  [3:0] B,
  input  C_in,
  output [3:0] Sum,
  output Carry
);

  wire _1bit_fulladder_1_carry, _1bit_fulladder_2_carry, _1bit_fulladder_3_carry, xor_1_out, xor_2_out,
       xor_3_out, xor_4_out;

  xor xor_1 (xor_1_out, B[0], C_in);
  xor xor_2 (xor_2_out, B[1], C_in);
  xor xor_3 (xor_3_out, B[2], C_in);
  xor xor_4 (xor_4_out, B[3], C_in);
  _1bit_fullAdder _1bit_fulladder_1 (
    .A(A[0]), .B(xor_1_out), .C_in(C_in), .Sum(Sum[0]), .Carry(_1bit_fulladder_1_carry));
  _1bit_fullAdder _1bit_fulladder_2 (
    .A(A[1]), .B(xor_2_out), .C_in(_1bit_fulladder_1_carry), .Sum(Sum[1]), .Carry(_1bit_fulladder_2_carry));
  _1bit_fullAdder _1bit_fulladder_3 (
    .A(A[2]), .B(xor_3_out), .C_in(_1bit_fulladder_2_carry), .Sum(Sum[2]), .Carry(_1bit_fulladder_3_carry));
  _1bit_fullAdder _1bit_fulladder_4 (
    .A(A[3]), .B(xor_4_out), .C_in(_1bit_fulladder_3_carry), .Sum(Sum[3]), .Carry(Carry));
endmodule
