// Digital circuit ControlUnit.dig as structural Verilog
module ControlUnit (
  input  A,
  input  B,
  input  C,
  input  D,
  output [1:0] WR,
  output WE,
  output IL,
  output ADD,
  output SUB,
  output AND,
  output OR,
  output XOR,
  output [1:0] RR_2,
  output [1:0] RR_1,
  output SLT,
  output PC
);

  wire and_5_out, and_6_out, and_7_out, and_8_out, not_2_out, not_3_out, not_4_out, or_1_out;

  and and_1 (SLT, A, B, C, not_3_out);
  and and_2 (PC, A, B, C, D);
  and and_3 (OR, A, B, not_4_out, not_3_out);
  and and_4 (AND, A, not_2_out, C, D);
  not not_1 (RR_1[0], A);
  not not_2 (not_2_out, B);
  not not_3 (not_3_out, D);
  not not_4 (not_4_out, C);
  and and_5 (and_5_out, RR_1[0], not_2_out, C);
  and and_6 (and_6_out, A, not_4_out, not_3_out);
  and and_7 (and_7_out, RR_1[0], C);
  and and_8 (and_8_out, RR_1[0], D);
  or or_1 (or_1_out, and_5_out, and_6_out);
  or or_2 (IL, and_7_out, and_8_out);
  or or_3 (WE, A, C, D);
  and and_9 (XOR, A, B, not_4_out, D);
  not not_5 (WR[0], or_1_out);
  and and_10 (ADD, A, not_2_out, not_4_out, D);
  and and_11 (SUB, A, not_2_out, C, not_3_out);

  assign RR_1[1] = 1'b0;
  assign RR_2 = 2'b01;
  assign WR[1] = 1'b0;
endmodule
