// Digital circuit FDE.dig as structural Verilog
module FDE (
  input  CLK,
  input  In,
  output [1:0] State
);

  wire and_1_out, and_2_out, and_3_out, and_4_out, not_1_out, not_2_out, not_3_out, not_4_out, or_1_out,
       or_2_out;

  not not_1 (not_1_out, State[1]);
  not not_2 (not_2_out, State[0]);
  and and_1 (and_1_out, State[1], not_3_out);
  not not_3 (not_3_out, In);
  and and_2 (and_2_out, State[0], In);
  and and_3 (and_3_out, not_1_out, not_2_out, In);
  and and_4 (and_4_out, State[0], not_4_out);
  not not_4 (not_4_out, In);
  or or_1 (or_1_out, and_1_out, and_2_out);
  or or_2 (or_2_out, and_3_out, and_4_out);
  D_FF Dmsb (.D(or_1_out), .C(CLK), .Q(State[1]));  // open: nQ
  D_FF Dlsb (.D(or_2_out), .C(CLK), .Q(State[0]));  // open: nQ
endmodule
