// Digital circuit FinalSubmission_4BIT_CPU_Circuit.dig as structural Verilog
module FinalSubmission_4BIT_CPU_Circuit (
  input  Clock,
  input  Load_Address,
  input  [3:0] JumpTo_Address,
  input  [1:0] Register_Selector,
  input  [3:0] Operation_Data,
  output [3:0] out_2,
  output SLT,
  output Zero,
  output [3:0] Output,
  output Carry,
  output [3:0] Register_A,
  output [3:0] Register_B,
  output [3:0] Instruction
);

  wire _4bit_fulladdersubtractor_1_carry, demultiplexer_1_out_0, demultiplexer_1_out_1,
       demultiplexer_1_out_2, demultiplexer_1_out_3, not_1_out, not_2_out;
  wire [3:0] _4bit_fulladdersubtractor_1_sum, demultiplexer_2_out_0, demultiplexer_2_out_1,
       demultiplexer_2_out_2, demultiplexer_2_out_3, multiplexer_1_out, RAM_16__4_d;

  _4bit_fullAdderSubtractor _4bit_fulladdersubtractor_1 (
    .A(out_2), .B(4'b0001), .C_in(1'b0), .Sum(_4bit_fulladdersubtractor_1_sum),
    .Carry(_4bit_fulladdersubtractor_1_carry));
  not not_1 (not_1_out, Clock);
  Multiplexer #(.Bits(4)) multiplexer_1 (
    .sel(Load_Address), .in_0(_4bit_fulladdersubtractor_1_sum), .in_1(JumpTo_Address), .out(multiplexer_1_out));
  Register #(.Bits(4)) PC (.D(multiplexer_1_out), .C(not_1_out), .en(not_1_out), .Q(out_2));
  BlockRAMDualPort #(.AddrBits(4), .Bits(4)) RAM_16__4 (
    .A(out_2), .Din(Operation_Data), .str(Clock), .C(Clock), .D(RAM_16__4_d));
  not not_2 (not_2_out, Clock);
  Demultiplexer #(.Selector_Bits(2)) demultiplexer_1 (
    .sel(Register_Selector), .in(1'b1), .out_0(demultiplexer_1_out_0), .out_1(demultiplexer_1_out_1),
    .out_2(demultiplexer_1_out_2), .out_3(demultiplexer_1_out_3));
  Demultiplexer #(.Selector_Bits(2), .Bits(4)) demultiplexer_2 (
    .sel(Register_Selector), .in(RAM_16__4_d), .out_0(demultiplexer_2_out_0), .out_1(demultiplexer_2_out_1),
    .out_2(demultiplexer_2_out_2), .out_3(demultiplexer_2_out_3));
  Register #(.Bits(4)) IR (.D(demultiplexer_2_out_0), .C(not_2_out), .en(demultiplexer_1_out_0), .Q(Instruction));
  Register #(.Bits(4)) A (.D(demultiplexer_2_out_1), .C(not_2_out), .en(demultiplexer_1_out_1), .Q(Register_A));
  Register #(.Bits(4)) B (.D(demultiplexer_2_out_2), .C(not_2_out), .en(demultiplexer_1_out_2), .Q(Register_B));
  FullALU fullalu_1 (
    .A(Register_A), .B(Register_B), .Selector(Instruction[2:0]), .Output(Output), .Carry(Carry),
    .Zero_Flag(Zero), .SLT_Flag(SLT));
  // also tied to GND on the sheet: {_4bit_fulladdersubtractor_1_carry, demultiplexer_2_out_3[0], demultiplexer_2_out_3[1], demultiplexer_2_out_3[2], demultiplexer_2_out_3[3], demultiplexer_1_out_3, Instruction[3]}

  // Notes on the sheet:
  //   Operation Dictionary: 
  //   0000 = Add
  //   0001 = Subtract
  //   0010 = AND
  //   0011 = OR
  //   0100 = XOR
  //   0101 = SLT
  //   0110 = Jump
  //   0111 = Load A
  //   1000 = Load B
  //   1001 = Load IR
  //   1010 = Store
  //   1011 = Branch if equal
  //   1100 = No operation
  //   1101 = No operation
  //   1110 = No operation 
  //   1111 = No operation
  //   Instruction Memory Addresses: 0000 - 1010
  //   Data Memory Addresses: 1011 - 1111
endmodule
