// Digital circuit FullALU.dig as structural Verilog
module FullALU (
  input  [3:0] A,
  input  [3:0] B,
  input  [2:0] Selector,
  output [3:0] Output,
  output Carry,
  output Zero_Flag,
  output SLT_Flag
);

  wire and_1_out, and_2_out, nor_1_out, nor_2_out, not_1_out;
  wire [0:0] bitselector_1_out;
  wire [3:0] _4bit_fulladdersubtractor_1_sum, and_3_out, or_1_out, xor_1_out;

  nor nor_1 (nor_1_out, Selector[2], Selector[1]);
  assign xor_1_out = B ^ A;  // XOr xor_1, 4 bits wide
  and and_1 (and_1_out, Selector[0], Selector[2]);
  and and_2 (and_2_out, nor_1_out, Selector[0]);
  assign or_1_out = B | A;  // Or or_1, 4 bits wide
  Multiplexer #(.Selector_Bits(3), .Bits(4)) multiplexer_1 (
    .sel(Selector), .in_0(_4bit_fulladdersubtractor_1_sum), .in_1(_4bit_fulladdersubtractor_1_sum),
    .in_2(and_3_out), .in_3(or_1_out), .in_4(xor_1_out), .in_5({3'b000, bitselector_1_out[0]}),
    .in_6(4'b0000), .in_7(4'b0000), .out(Output));
  not not_1 (not_1_out, Selector[1]);
  BitSelector #(.Selector_Bits(2)) bitselector_1 (
    .in(_4bit_fulladdersubtractor_1_sum), .sel(2'b11), .out(bitselector_1_out[0]));
  assign and_3_out = B & A;  // And and_3, 4 bits wide
  and and_4 (SLT_Flag, not_1_out, and_1_out);
  _4bit_fullAdderSubtractor _4bit_fulladdersubtractor_1 (
    .A(A), .B(B), .C_in(Selector[0]), .Sum(_4bit_fulladdersubtractor_1_sum), .Carry(Carry));
  nor nor_2 (nor_2_out, _4bit_fulladdersubtractor_1_sum[0], _4bit_fulladdersubtractor_1_sum[1], _4bit_fulladdersubtractor_1_sum[2], _4bit_fulladdersubtractor_1_sum[3]);
  and and_5 (Zero_Flag, and_2_out, nor_2_out);
endmodule
