// Digital circuit InstructionReg.dig as structural Verilog
module InstructionReg (
  input  CLK,
  input  [1:0] Con,
  input  [3:0] Op,
  output NOP,
  output MovA,
  output MovB,
  output MovA_B,
  output MovB_A,
  output AddA_B,
  output SubA_B,
  output AndA_B,
  output OrA_B,
  output XorA_B,
  output SLTA_B
);

  wire decoder_1_out_11;
  wire [3:0] register_1_out;

  Register register_1 (.In(Op), .Con(Con), .CLK(CLK), .Out(register_1_out));
  Decoder #(.Selector_Bits(4)) decoder_1 (
    .sel(register_1_out), .out_0(NOP), .out_1(MovA), .out_2(MovB), .out_3(MovA_B), .out_4(MovB_A),
    .out_5(AddA_B), .out_6(SubA_B), .out_7(AndA_B), .out_8(OrA_B), .out_9(XorA_B), .out_10(SLTA_B),
    .out_11(decoder_1_out_11), .out_12(decoder_1_out_11), .out_13(decoder_1_out_11),
    .out_14(decoder_1_out_11), .out_15(decoder_1_out_11));
  // also tied to GND on the sheet: decoder_1_out_11
endmodule
