// Digital circuit MemoryModule.dig as structural Verilog
module MemoryModule (
  input  [1:0] R_W_C,
  input  CLK,
  input  [3:0] Address,
  input  [3:0] Data,
  output [3:0] Out
);

  wire [3:0] _0_out, _1_out, _2_out, _3_out, _4_out, _5_out, _6_out, _7_out, _8_out, _9_out, _10_out,
       _11_out, _12_out, _13_out, _14_out, _15_out, demultiplexer_1_out_0, demultiplexer_1_out_1,
       demultiplexer_1_out_2, demultiplexer_1_out_3, demultiplexer_1_out_4, demultiplexer_1_out_5,
       demultiplexer_1_out_6, demultiplexer_1_out_7, demultiplexer_1_out_8, demultiplexer_1_out_9,
       demultiplexer_1_out_10, demultiplexer_1_out_11, demultiplexer_1_out_12, demultiplexer_1_out_13,
       demultiplexer_1_out_14, demultiplexer_1_out_15;

  Demultiplexer #(.Selector_Bits(4), .Bits(4)) demultiplexer_1 (
    .sel(Address), .in(Data), .out_0(demultiplexer_1_out_0), .out_1(demultiplexer_1_out_1),
    .out_2(demultiplexer_1_out_2), .out_3(demultiplexer_1_out_3), .out_4(demultiplexer_1_out_4),
    .out_5(demultiplexer_1_out_5), .out_6(demultiplexer_1_out_6), .out_7(demultiplexer_1_out_7),
    .out_8(demultiplexer_1_out_8), .out_9(demultiplexer_1_out_9), .out_10(demultiplexer_1_out_10),
    .out_11(demultiplexer_1_out_11), .out_12(demultiplexer_1_out_12), .out_13(demultiplexer_1_out_13),
    .out_14(demultiplexer_1_out_14), .out_15(demultiplexer_1_out_15));
  Register _0 (.In(demultiplexer_1_out_0), .Con(R_W_C), .CLK(CLK), .Out(_0_out));
  Register _1 (.In(demultiplexer_1_out_1), .Con(R_W_C), .CLK(CLK), .Out(_1_out));
  Register _2 (.In(demultiplexer_1_out_2), .Con(R_W_C), .CLK(CLK), .Out(_2_out));
  Register _3 (.In(demultiplexer_1_out_3), .Con(R_W_C), .CLK(CLK), .Out(_3_out));
  Register _4 (.In(demultiplexer_1_out_4), .Con(R_W_C), .CLK(CLK), .Out(_4_out));
  Register _5 (.In(demultiplexer_1_out_5), .Con(R_W_C), .CLK(CLK), .Out(_5_out));
  Register _6 (.In(demultiplexer_1_out_6), .Con(R_W_C), .CLK(CLK), .Out(_6_out));
  Register _7 (.In(demultiplexer_1_out_7), .Con(R_W_C), .CLK(CLK), .Out(_7_out));
  Register _8 (.In(demultiplexer_1_out_8), .Con(R_W_C), .CLK(CLK), .Out(_8_out));
  Register _9 (.In(demultiplexer_1_out_9), .Con(R_W_C), .CLK(CLK), .Out(_9_out));
  Register _10 (.In(demultiplexer_1_out_10), .Con(R_W_C), .CLK(CLK), .Out(_10_out));
  Register _11 (.In(demultiplexer_1_out_11), .Con(R_W_C), .CLK(CLK), .Out(_11_out));
  Register _12 (.In(demultiplexer_1_out_12), .Con(R_W_C), .CLK(CLK), .Out(_12_out));
  Register _13 (.In(demultiplexer_1_out_13), .Con(R_W_C), .CLK(CLK), .Out(_13_out));
  Register _14 (.In(demultiplexer_1_out_14), .Con(R_W_C), .CLK(CLK), .Out(_14_out));
  Register _15 (.In(demultiplexer_1_out_15), .Con(R_W_C), .CLK(CLK), .Out(_15_out));
  Multiplexer #(.Selector_Bits(4), .Bits(4)) multiplexer_1 (
    .sel(Address), .in_0(_0_out), .in_1(_1_out), .in_2(_2_out), .in_3(_3_out), .in_4(_4_out), .in_5(_5_out),
    .in_6(_6_out), .in_7(_7_out), .in_8(_8_out), .in_9(_9_out), .in_10(_10_out), .in_11(_11_out),
    .in_12(_12_out), .in_13(_13_out), .in_14(_14_out), .in_15(_15_out), .out(Out));
endmodule
