// Digital circuit ProgramCounter.dig as structural Verilog
module ProgramCounter (
  input  CLK,
  input  [1:0] Con2,
  input  [3:0] Address,
  input  Con1,
  output [3:0] Out
);

  wire [3:0] _4bit_full_adder_1_p4, multiplexer_1_out;

  Multiplexer #(.Bits(4)) multiplexer_1 (
    .sel(Con1), .in_0(_4bit_full_adder_1_p4), .in_1(Address), .out(multiplexer_1_out));
  // Register register_1: pin names not known; wires that end beside it: multiplexer_1_out, Con2, CLK, Out
  // _4bit_full_adder _4bit_full_adder_1: pin names not known; wires that end beside it: Out, 4'b0001, 1'b0, _4bit_full_adder_1_p4
endmodule
