// Digital circuit Register.dig as structural Verilog
module Register (
  input  [3:0] In,
  input  [1:0] Con,
  input  CLK,
  output [3:0] Out
);

  wire [3:0] multiplexer_1_out;

  Multiplexer #(.Bits(4), .Selector_Bits(2)) multiplexer_1 (
    .sel(Con), .in_0(Out), .in_1(In), .in_2(4'b0000), .in_3(4'b0000), .out(multiplexer_1_out));
  D_FF d_ff_1 (.D(multiplexer_1_out[0]), .C(CLK), .Q(Out[0]));  // open: nQ
  D_FF d_ff_2 (.D(multiplexer_1_out[1]), .C(CLK), .Q(Out[1]));  // open: nQ
  D_FF d_ff_3 (.D(multiplexer_1_out[2]), .C(CLK), .Q(Out[2]));  // open: nQ
  D_FF d_ff_4 (.D(multiplexer_1_out[3]), .C(CLK), .Q(Out[3]));  // open: nQ
endmodule
