// Digital circuit RegistersFile.dig as structural Verilog
module RegistersFile (
  input  [1:0] Read1,
  input  [1:0] Read2,
  input  CLK,
  input  [3:0] WD,
  input  [1:0] WR,
  input  [1:0] Con,
  output [3:0] Data1,
  output [3:0] Data2
);

  wire [3:0] A_out, B_out, C_out, D_out, demultiplexer_1_out_0, demultiplexer_1_out_1, demultiplexer_1_out_2,
       demultiplexer_1_out_3;

  Demultiplexer #(.Bits(4), .Selector_Bits(2)) demultiplexer_1 (
    .sel(WR), .in(WD), .out_0(demultiplexer_1_out_0), .out_1(demultiplexer_1_out_1),
    .out_2(demultiplexer_1_out_2), .out_3(demultiplexer_1_out_3));
  Register A (.In(demultiplexer_1_out_0), .Con(Con), .CLK(CLK), .Out(A_out));
  Register B (.In(demultiplexer_1_out_1), .Con(Con), .CLK(CLK), .Out(B_out));
  Register C (.In(demultiplexer_1_out_2), .Con(Con), .CLK(CLK), .Out(C_out));
  Register D (.In(demultiplexer_1_out_3), .Con(Con), .CLK(CLK), .Out(D_out));
  Multiplexer #(.Bits(4), .Selector_Bits(2)) multiplexer_1 (
    .sel(Read1), .in_0(A_out), .in_1(B_out), .in_2(C_out), .in_3(D_out), .out(Data1));
  Multiplexer #(.Bits(4), .Selector_Bits(2)) multiplexer_2 (
    .sel(Read2), .in_0(A_out), .in_1(B_out), .in_2(C_out), .in_3(D_out), .out(Data2));
endmodule
